# Fritzing sketch schema (saved by Fritzing 0.9.3b)
breadboards: 1

parts:
  Part1 = Arduino Nano (Rev3.0) (ICSP)
  M1 = gy9250

nets:
  N1: Part1.GND, M1.pin2
  N2: Part1.A5, M1.pin3
  N3: Part1.A4, M1.pin4
  N4: Part1.3V3, M1.pin1

custom parts:
  gy9250: MPU-9250 module (three-axis gyroscope + three-axis acceleration + three-axis magnetic field). The generic model from ebay et. al. rather than the Sparkfun version.
